// Logisim project circuit.circ as structural Verilog: 6 circuits, main circuit main
module main (
);

  wire and_4_out, and_5_out, and_6_out, and_7_out, CLEAR, CLK, CS1ACTIVE, CS2ACTIVE, ESC, not_2_out,
       not_3_out, not_4_out, not_5_out, not_6_out, not_7_out, not_8_out, not_9_out, not_10_out, not_11_out,
       not_12_out, not_13_out, not_14_out, not_15_out, or_1_out, or_2_out, RAMACTIVE, READ, RESET, ROMACTIVE,
       S2, S6, SERACTIVE, TIMERACTIVE, WRITE;
  wire [6:0] D1, D2, D3, D4, D5, S3;
  wire [7:0] bit_extender_1_out, controlled_buffer_9_out, controlled_buffer_10_out, DATA, multiplexer_1_out,
       ram_1_dout, rom_2_data;
  wire [7:1] CS1ADDRS_data, rom_1_data;
  wire [15:0] ADDR;

  ROM #(.addrWidth(16)) CS1ADDRS (.addr(ADDR), .data({CS1ADDRS_data, CS1ACTIVE}));
  LED led_1 (.in(RESET));
  Clock clock_1 (.out(CLK));
  // NOT_Gate not_1 has open pins: in=RESET, out=open
  and and_1 (S2, SERACTIVE, READ);
  // W65C02S__Simple w65c02s_simple_1: pin names not known; wires that end beside it: RESET, CLK, READ, DATA, ADDR
  not not_2 (not_2_out, ADDR[0]);
  not not_3 (not_3_out, ADDR[2]);
  not not_4 (not_4_out, ADDR[3]);
  not not_5 (not_5_out, ADDR[4]);
  not not_6 (not_6_out, ADDR[5]);
  not not_7 (not_7_out, ADDR[6]);
  not not_8 (not_8_out, ADDR[7]);
  not not_9 (not_9_out, ADDR[8]);
  not not_10 (not_10_out, ADDR[9]);
  not not_11 (not_11_out, ADDR[10]);
  not not_12 (not_12_out, ADDR[11]);
  not not_13 (not_13_out, ADDR[12]);
  not not_14 (not_14_out, ADDR[13]);
  not not_15 (not_15_out, ADDR[14]);
  and and_2 (S6, SERACTIVE, WRITE);
  PLA #(.in_width(8), .out_width(1), .\table ("00010001 1 # Device Control 1")) pla_1 (.in(DATA), .out(CLEAR));
  ROM #(.addrWidth(16)) rom_1 (.addr(ADDR), .data({rom_1_data, CS2ACTIVE}));
  assign bit_extender_1_out = {{1{1'b0}}, S3};  // Bit_Extender bit_extender_1
  Multiplexer #(.width(8)) multiplexer_1 (.in0(bit_extender_1_out), .in1(8'h1b), .out(multiplexer_1_out), .sel(ESC));
  and and_3 (SERACTIVE, not_2_out, ADDR[1], not_3_out, not_4_out, not_5_out, not_6_out, not_7_out, not_8_out, not_9_out, not_10_out, not_11_out, not_12_out, not_13_out, not_14_out, not_15_out, ADDR[15]);
  not not_16 (WRITE, READ);
  assign DATA = and_4_out ? multiplexer_1_out : 8'bz;  // Controlled_Buffer controlled_buffer_1
  and and_4 (and_4_out, SERACTIVE, READ);
  assign D1 = WRITE ? 7'b0111110 : 7'bz;  // Controlled_Buffer controlled_buffer_2
  TTY #(.cols(58), .rows(16), .trigger("falling")) tty_1 (.data(DATA[6:0]), .clk(CLK), .we(S6), .clr(CLEAR));
  DotMatrix dotmatrix_1 (.col0(D1), .col1(D2), .col2(D3), .col3(D4), .col4(D5));
  assign D3 = WRITE ? 7'b0001110 : 7'bz;  // Controlled_Buffer controlled_buffer_3
  assign D2 = WRITE ? 7'b0000001 : 7'bz;  // Controlled_Buffer controlled_buffer_4
  Keyboard #(.buflen(31), .trigger("falling")) keyboard_1 (.clk(CLK), .re(S2), .data(S3));  // open: clr, avail
  assign D5 = WRITE ? 7'b0111110 : 7'bz;  // Controlled_Buffer controlled_buffer_5
  assign D4 = WRITE ? 7'b0000001 : 7'bz;  // Controlled_Buffer controlled_buffer_6
  not not_17 (RAMACTIVE, ADDR[15]);
  assign DATA = RAMACTIVE ? controlled_buffer_10_out : 8'bz;  // Controlled_Buffer controlled_buffer_7
  assign DATA = and_5_out ? rom_2_data : 8'bz;  // Controlled_Buffer controlled_buffer_8
  and and_5 (and_5_out, READ, ROMACTIVE);
  or or_1 (or_1_out, ADDR[13], ADDR[2], ADDR[3], ADDR[4], ADDR[5], ADDR[6], ADDR[8], ADDR[9], ADDR[10], ADDR[11], ADDR[12], ADDR[7]);
  and and_6 (and_6_out, ADDR[0], ADDR[1]);
  Button button_1 (.out(ESC));
  Hex_Digit_Display hex_digit_display_1 (.value(ADDR[15:12]));  // open: dp
  Hex_Digit_Display CLOCK_1_dup2 (.value(ADDR[11:8]));  // open: dp
  RAM #(.addrWidth(15)) ram_1 (
    .addr(ADDR[14:0]), .we(WRITE), .oe(RAMACTIVE), .clk(CLK), .din(controlled_buffer_9_out), .dout(ram_1_dout));
  assign controlled_buffer_9_out = WRITE ? DATA : 8'bz;  // Controlled_Buffer controlled_buffer_9
  ROM #(.addrWidth(16)) rom_2 (.addr(ADDR), .data(rom_2_data));
  and and_7 (and_7_out, ADDR[14], ADDR[15]);
  or or_2 (or_2_out, or_1_out, and_6_out);
  Button button_2 (.out(CLEAR));
  Hex_Digit_Display hex_digit_display_2 (.value(ADDR[7:4]));  // open: dp
  Hex_Digit_Display hex_digit_display_3 (.value(ADDR[3:0]));  // open: dp
  Hex_Digit_Display hex_digit_display_4 (.value(DATA[7:4]));  // open: dp
  Hex_Digit_Display hex_digit_display_5 (.value(DATA[3:0]));  // open: dp
  assign controlled_buffer_10_out = READ ? ram_1_dout : 8'bz;  // Controlled_Buffer controlled_buffer_10
  and and_8 (ROMACTIVE, and_7_out, or_2_out);
  assign D1 = READ ? {7{1'b1}} : 7'bz;  // Controlled_Buffer controlled_buffer_11
  Button button_3 (.out(RESET));
  assign D4 = READ ? 7'b0110111 : 7'bz;  // Controlled_Buffer controlled_buffer_12
  assign D3 = READ ? 7'b1001000 : 7'bz;  // Controlled_Buffer controlled_buffer_13
  assign D2 = READ ? 7'b1001000 : 7'bz;  // Controlled_Buffer controlled_buffer_14
  LED led_2 (.in(CLK));
  LED led_3 (.in(RAMACTIVE));
  LED led_4 (.in(CS1ACTIVE));
  LED led_5 (.in(CS2ACTIVE));
  LED led_6 (.in(SERACTIVE));
  LED led_7 (.in(TIMERACTIVE));
  LED led_8 (.in(ROMACTIVE));
  assign D5 = READ ? {7{1'b0}} : 7'bz;  // Controlled_Buffer controlled_buffer_15
  PongCart pongcart_1 (.A(ADDR), .CS(CS1ACTIVE), .RW(READ), .DOUT(DATA));
  EditorCart editorcart_1 ();  // open: RW, CS, A, DOUT
  CalcCart calccart_1 ();  // open: A, CS, RW, DOUT
  VideoCart videocart_1 ();  // open: A, RW, CS, CLK, DIN, O1, O2, O3, O4, O5, O6
  // RGB_Video #(.height(16), .scale(5), .width(16)) rgb_video_1: pin names not known; wires that end beside it: ADDR, READ, CS2ACTIVE, CLK, DATA

  // Other names for the same wires on the sheet: S5[6:0] = DATA[6:0]; S1 = CLK; S4 = CLK; S7 = CLEAR

  // Notes on the sheet:
  //   CPU
  //   contents of CS1ADDRS (hex, n*v repeats v):
  //   32771*0 8192*1
  //   6502 Microprocessor
  //   SERIAL 0x8002
  //   Equality Comparator
  //   Cartridge Slots
  //   ROM Decoders 
  //   Ozpex 64
  //   A fictional 8-bit computer based on the 6502
  //   github.com/BeauConstrictor/Ozpex-64
  //   contents of rom_1 (hex, n*v repeats v):
  //   40963*0 8192*1
  //   TODO:
  //   Fix clearing
  //   !A15
  //   RAM 0x0000 -> 0x7FFF
  //   ROM 0xC003 -> 0xFFFF
  //   Read/Write Display
  //   Control Panel
  //   (A14 & A15) & ((A2 | ... | A13) | (A0 & A1))
  //   contents of rom_2 (hex, n*v repeats v):
  //   49155*0 a9 69 85 50 a9 c1 85 51 20 5b c1 20 25 c0 20 4c c1 a0 0 91 30 20 1e c0 4c 11 c0 e6 30 d0 2
  //   e6 31 60 a5 31 20 3b c1 8e 2 80 8c 2 80 a5 30 20 3b c1 8e 2 80 8c 2 80 a9 3a 8d 2 80 a9 20 8d 2 80
  //   60 ad 2 80 f0 fb c9 40 f0 1e c9 3e f0 67 8d 2 80 c9 78 f0 52 c9 20 f0 e8 c9 a f0 5 c9 3b f0 26 60 20
  //   25 c0 4c 46 c0 a9 a 8d 2 80 8d 2 80 20 4c c1 85 31 20 4c c1 85 30 a9 3a 8d 2 80 a9 20 8d 2 80 4c 46
  //   c0 ad 2 80 8d 2 80 c9 a f0 d1 c9 7f d0 f2 a9 8 8d 2 80 a9 20 8d 2 80 a9 8 8d 2 80 4c 8c c0 a9 a 8d 2
  //   80 20 b7 c0 6c f8 ff 6c 30 0 a9 8e 85 50 a9 c1 85 51 20 5b c1 20 4c c1 85 33 20 4c c1 85 32 a9 3a 8d
  //   2 80 a9 a 8d 2 80 20 25 c0 4c ed c0 a5 30 29 f d0 8 a9 a 8d 2 80 20 25 c0 a0 0 b1 30 20 3b c1 8e 2
  //   80 8c 2 80 a9 20 8d 2 80 a5 30 c5 32 f0 6 20 1e c0 4c df c0 a5 31 c5 33 f0 3 4c 5 c1 a9 a 8d 2 80 8d
  //   2 80 20 25 c0 4c 11 c0 20 46 c0 c9 3a 90 4 38 e9 57 60 e9 2f 60 c9 a 90 4 18 69 57 60 69 30 60 48
  //   4*4a 20 30 c1 aa 68 29 f 20 30 c1 a8 60 20 22 c1 4*a 85 40 20 22 c1 5 40 60 a0 0 b1 50 f0 7 8d 2 80
  //   c8 4c 5d c1 60 11 4*2a 20 4f 7a 70 65 78 20 36 34 20 4d 6f 6e 69 74 6f 72 20 76 32 2e 30 2e 30 20
  //   4*2a a a 0 8 8 20 20 8 8 20 2d 3e 20 15968*0 e c0 0 0 3 c0
endmodule

module BBSRAM (
  input  [15:0] A,
  input  RW,
  input  CS,
  input  CLK,
  input  [7:0] DIN,
  output [7:0] DOUT
);

  wire not_1_out;

  not not_1 (not_1_out, RW);
  RAM #(.addrWidth(16), .\type ("nonvolatile")) ram_1 (
    .addr(A), .we(not_1_out), .oe(CS), .clk(CLK), .din(DIN), .dout(DOUT));
endmodule

module CalcCart (
  input  [15:0] A,
  input  CS,
  input  RW,
  output [7:0] DOUT
);

  wire and_1_out;
  wire [7:0] rom_1_data;

  and and_1 (and_1_out, RW, CS);
  assign DOUT = and_1_out ? rom_1_data : 8'bz;  // Controlled_Buffer controlled_buffer_1
  ROM #(.addrWidth(16)) rom_1 (.addr(A), .data(rom_1_data));

  // Notes on the sheet:
  //   contents of rom_1 (hex, n*v repeats v):
  //   32771*0 a9 b0 85 50 a9 80 85 51 20 a2 80 20 14 80 4c e 80 20 93 80 85 30 20 50 80 85 20 20 93 80 85
  //   10 a9 12 85 50 a9 81 85 51 20 a2 80 a5 20 c9 2b f0 8 a5 30 38 e5 10 4c 41 80 a5 30 18 65 10 20 82 80
  //   8e 2 80 8c 2 80 a9 a 8d 2 80 60 ad 2 80 f0 fb c9 1b f0 8 8d 2 80 c9 20 f0 f0 60 a9 a 8d 2 80 4c f8
  //   ff 20 50 80 c9 3a 90 4 38 e9 57 60 e9 2f 60 c9 a 90 4 18 69 57 60 69 30 60 48 4*4a 20 77 80 aa 68 29
  //   f 20 77 80 a8 60 20 69 80 4*a 85 40 20 69 80 5 40 60 a0 0 b1 50 f0 7 8d 2 80 c8 4c a4 80 60 11 1b 5b
  //   37 6d 20 4f 36 34 20 43 61 6c 63 75 6c 61 74 6f 72 20 76 31 2e 30 2e 30 20 1b 5b 30 6d a 54 49 50 3a
  //   20 53 70 61 63 65 73 20 61 72 65 20 6f 70 74 69 6f 6e 61 6c 2e a a 45 78 61 6d 70 6c 65 73 3a a 30
  //   31 20 2b 20 30 32 20 3d 20 30 33 a 61 35 20 2d 20 30 32 20 3d 20 61 33 a a 0 20 3d 20
endmodule

module EditorCart (
  input  RW,
  input  [15:0] A,
  input  CS,
  output [7:0] DOUT
);

  wire and_1_out;
  wire [7:0] rom_1_data;

  assign DOUT = and_1_out ? rom_1_data : 8'bz;  // Controlled_Buffer controlled_buffer_1
  and and_1 (and_1_out, CS, RW);
  ROM #(.addrWidth(16)) rom_1 (.addr(A), .data(rom_1_data));
  CalcCart calccart_1 ();  // open: A, CS, RW, DOUT

  // Notes on the sheet:
  //   contents of rom_1 (hex, n*v repeats v):
  //   32771*0 20 3d 80 20 79 80 20 31 80 ad 2 80 f0 fb c9 1b f0 13 20 42 80 c9 7f f0 6 8d 2 80 4c c 80 20
  //   31 80 4c c 80 20 66 80 a9 a 8d 2 80 60 a9 11 8d 2 80 20 91 80 20 58 80 60 a9 0 85 20 60 c9 7f f0 9
  //   a6 20 e8 9d 1 2 e6 20 60 c6 20 c9 0 d0 2 e6 20 60 a2 ff e8 bd 1 2 8d 2 80 e4 20 d0 f5 60 a2 ff e8 bd
  //   1 2 9d 3 a0 a5 20 8d 2 c0 e4 20 d0 f0 60 ad 2 c0 85 20 a2 ff e8 bd 3 a0 9d 1 2 a5 20 8d 2 c0 e4 20
  //   d0 f0 60 a2 0 bd a0 80 f0 7 8d 2 80 e8 4c 93 80 60 1b 5b 37 6d 20 4f 36 34 20 45 64 69 74 6f 72 20
  //   76 31 2e 30 2e 30 20 1b 5b 30 6d a 54 49 50 3a 20 70 72 65 73 73 20 45 53 43 20 74 6f 20 73 61 76 65
  //   20 74 6f 20 43 53 32 20 61 6e 64 20 71 75 69 74 2e a a
endmodule

module VideoCart (
  input  [15:0] A,
  input  RW,
  input  CS,
  input  CLK,
  input  [7:0] DIN,
  output O1,
  output O2,
  output O3,
  output [3:0] O4,
  output [3:0] O5,
  output [7:0] O6
);

  wire controlled_buffer_2_out;
  wire [15:0] controlled_buffer_1_out;

  assign {controlled_buffer_1_out[15:12], O4, O5, controlled_buffer_1_out[3:0]} = CS ? A : 16'bz;  // Controlled_Buffer controlled_buffer_1
  assign controlled_buffer_2_out = CS ? RW : 1'bz;  // Controlled_Buffer controlled_buffer_2
  assign O2 = CS ? CLK : 1'bz;  // Controlled_Buffer controlled_buffer_3
  assign O6 = CS ? DIN : 8'bz;  // Controlled_Buffer controlled_buffer_4
  not not_1 (O3, controlled_buffer_2_out);
  PLA #(.in_width(16), .out_width(1), .\table ("1100000000000010 1 # Clear Display")) pla_1 (
    .in({controlled_buffer_1_out[15:12], O4, O5, controlled_buffer_1_out[3:0]}), .out(O1));
endmodule

module PongCart (
  input  [15:0] A,
  input  CS,
  input  RW,
  output [7:0] DOUT
);

  wire and_1_out;
  wire [7:0] rom_1_data;

  CalcCart calccart_1 ();  // open: A, CS, RW, DOUT
  and and_1 (and_1_out, RW, CS);
  assign DOUT = and_1_out ? rom_1_data : 8'bz;  // Controlled_Buffer controlled_buffer_1
  ROM #(.addrWidth(16)) rom_1 (.addr(A), .data(rom_1_data));

  // Notes on the sheet:
  //   contents of rom_1 (hex, n*v repeats v):
  //   32771*0 a9 7 85 30 85 32 85 33 a9 0 85 36 85 37 85 34 85 35 20 32 81 20 f 81 20 4b 80 20 84 80 10*ea
  //   e6 36 4c 15 80 a9 8c 85 38 a9 81 85 39 20 68 81 ad 2 80 c9 a d0 f9 8d 2 80 8d 2 80 6c f8 ff a5 32 c9
  //   f 90 8 a9 1 85 34 c6 32 c6 32 a5 32 c9 1 b0 10 a5 33 c5 30 d0 cb e6 37 a9 0 85 34 e6 32 e6 32 a5 33
  //   c9 f 90 4 a9 0 85 35 a5 33 c9 1 b0 4 a9 1 85 35 60 a9 7a 85 38 a9 81 85 39 20 68 81 a5 37 20 57 81
  //   e0 30 f0 3 8e 2 80 8c 2 80 a9 a 8d 2 80 a0 0 a9 83 85 38 a9 81 85 39 20 68 81 a2 0 e4 32 d0 12 c4 33
  //   d0 e a9 a6 85 38 a9 81 85 39 20 68 81 4c fa 80 e0 0 d0 11 c4 30 d0 d a9 20 8d 2 80 a9 7c 8d 2 80 4c
  //   fa 80 e0 f d0 11 c4 33 d0 d a9 7c 8d 2 80 a9 20 8d 2 80 4c fa 80 a9 20 8d 2 80 8d 2 80 e8 e0 10 d0
  //   b3 a9 87 85 38 a9 81 85 39 20 68 81 c8 c0 10 d0 96 a5 36 29 1 d0 1c a5 34 f0 5 c6 32 4c 20 81 e6 32
  //   a5 36 29 3 d0 b a5 34 a5 35 f0 3 e6 33 60 c6 33 60 ad 2 80 c9 77 f0 5 c9 73 f0 6 60 c6 30 4c 45 81
  //   e6 30 a5 30 29 f 85 30 60 c9 a 90 4 18 69 57 60 69 30 60 48 4*4a 20 4c 81 aa 68 29 f 20 4c 81 a8 60
  //   98 48 a0 0 b1 38 f0 7 8d 2 80 c8 4c 6c 81 68 a8 60 11 53 63 6f 72 65 3a 20 0 7c 7c 20 0 20 7c 7c a 0
  //   47 61 6d 65 20 6f 76 65 72 21 20 28 70 72 65 73 73 20 65 6e 74 65 72 29 20 0 23 23
endmodule
